// Logisim project Projeto trbalho m2.circ as structural Verilog: 3 circuits, main circuit main
module main (
  input  in_1
);

  wire and_1_out, and_2_out, and_3_out, and_4_out, and_5_out, and_6_out, and_7_out, and_8_out, clock_1_out,
       clock_2_out, clock_3_out, comparador_1_sc1, comparador_1_sc2, comparador_1_sc3, comparador_1_sc4,
       comparador_1_sc5, comparador_1_sc6, comparador_1_sc7, comparador_1_sc8, comparador_1_sc9,
       comparador_1_sc10, comparador_1_sc11, comparador_1_sc12, comparador_1_sc13, comparador_1_sc14,
       comparador_1_sc15, comparador_1_sc16, comparador_1_sc17, comparador_1_sc18, comparador_1_sc19,
       comparador_1_sc20, comparador_1_sc21, comparador_1_sc22, comparador_1_sc23, comparador_1_sc24,
       comparador_1_sc25, comparador_1_sc26, comparador_1_sc27, comparador_1_sc28, comparador_1_sc29,
       comparador_1_sc30, comparador_1_sc31, comparador_1_sc32, not_1_out, not_2_out, not_3_out, not_4_out,
       not_5_out, not_6_out, not_7_out, or_1_out;
  wire [1:0] joystick_1_x, joystick_1_y;
  wire [4:0] counter_1_q, counter_2_q, not_8_out, random_1_out, random_2_out;
  wire [31:0] comparador_1_s1, comparador_1_s2, comparador_1_s3, comparador_1_s4, comparador_1_s5,
       comparador_1_s6, comparador_1_s7, comparador_1_s8, comparador_1_s9, comparador_1_s10,
       comparador_1_s11, comparador_1_s12, comparador_1_s13, comparador_1_s14, comparador_1_s15,
       comparador_1_s16, comparador_1_s17, comparador_1_s18, comparador_1_s19, comparador_1_s20,
       comparador_1_s21, comparador_1_s22, comparador_1_s23, comparador_1_s24, comparador_1_s25,
       comparador_1_s26, comparador_1_s27, comparador_1_s28, comparador_1_s29, comparador_1_s30,
       comparador_1_s31, comparador_1_s32, decoder_1_out0, decoder_2_out0, demultiplexer_1_out0,
       demultiplexer_1_out1, demultiplexer_1_out2, demultiplexer_1_out3, demultiplexer_1_out4,
       demultiplexer_1_out5, demultiplexer_1_out6, demultiplexer_1_out7, demultiplexer_1_out8,
       demultiplexer_1_out9, demultiplexer_1_out10, demultiplexer_1_out11, demultiplexer_1_out12,
       demultiplexer_1_out13, demultiplexer_1_out14, demultiplexer_1_out15, demultiplexer_1_out16,
       demultiplexer_1_out17, demultiplexer_1_out18, demultiplexer_1_out19, demultiplexer_1_out20,
       demultiplexer_1_out21, demultiplexer_1_out22, demultiplexer_1_out23, demultiplexer_1_out24,
       demultiplexer_1_out25, demultiplexer_1_out26, demultiplexer_1_out27, demultiplexer_1_out28,
       demultiplexer_1_out29, demultiplexer_1_out30, demultiplexer_1_out31, demultiplexer_2_out0,
       demultiplexer_2_out1, demultiplexer_2_out2, demultiplexer_2_out3, demultiplexer_2_out4,
       demultiplexer_2_out5, demultiplexer_2_out6, demultiplexer_2_out7, demultiplexer_2_out8,
       demultiplexer_2_out9, demultiplexer_2_out10, demultiplexer_2_out11, demultiplexer_2_out12,
       demultiplexer_2_out13, demultiplexer_2_out14, demultiplexer_2_out15, demultiplexer_2_out16,
       demultiplexer_2_out17, demultiplexer_2_out18, demultiplexer_2_out19, demultiplexer_2_out20,
       demultiplexer_2_out21, demultiplexer_2_out22, demultiplexer_2_out23, demultiplexer_2_out24,
       demultiplexer_2_out25, demultiplexer_2_out26, demultiplexer_2_out27, demultiplexer_2_out28,
       demultiplexer_2_out29, demultiplexer_2_out30, demultiplexer_2_out31;

  Clock clock_1 (.out(clock_1_out));
  not not_1 (not_1_out, in_1);
  Clock clock_2 (.out(clock_2_out));
  not not_2 (not_2_out, joystick_1_x[1]);
  not not_3 (not_3_out, joystick_1_x[0]);
  and and_1 (and_1_out, not_3_out, joystick_1_x[1]);
  not not_4 (not_4_out, joystick_1_y[0]);
  and and_2 (and_2_out, not_4_out, joystick_1_y[1]);
  not not_5 (not_5_out, and_2_out);
  and and_3 (and_3_out, clock_2_out, or_1_out);
  and and_4 (and_4_out, joystick_1_x[0], not_2_out);
  not not_6 (not_6_out, and_1_out);
  and and_5 (and_5_out, clock_1_out, not_5_out);
  and and_6 (and_6_out, joystick_1_y[0], not_7_out);
  not not_7 (not_7_out, joystick_1_y[1]);
  Random #(.width(5), .seed(1991), .trigger("falling")) random_1 (
    .clk(and_3_out), .out(random_1_out));  // open: next, clr
  and and_7 (and_7_out, not_6_out, clock_1_out);
  Counter #(.width(5), .max('h1f)) counter_1 (
    .load(and_6_out), .Q(counter_1_q), .clk(and_5_out), .clr(in_1));  // open: D, count, carry
  Counter #(.width(5), .max('h1f)) counter_2 (
    .load(and_4_out), .Q(counter_2_q), .clk(and_7_out), .clr(in_1));  // open: D, count, carry
  assign not_8_out = ~counter_1_q;  // NOT_Gate not_8, 5 bits wide
  Decoder #(.select(5)) decoder_1 (
    .out0(decoder_1_out0[0]), .out1(decoder_1_out0[1]), .out2(decoder_1_out0[2]), .out3(decoder_1_out0[3]),
    .out4(decoder_1_out0[4]), .out5(decoder_1_out0[5]), .out6(decoder_1_out0[6]), .out7(decoder_1_out0[7]),
    .out8(decoder_1_out0[8]), .out9(decoder_1_out0[9]), .out10(decoder_1_out0[10]),
    .out11(decoder_1_out0[11]), .out12(decoder_1_out0[12]), .out13(decoder_1_out0[13]),
    .out14(decoder_1_out0[14]), .out15(decoder_1_out0[15]), .out16(decoder_1_out0[16]),
    .out17(decoder_1_out0[17]), .out18(decoder_1_out0[18]), .out19(decoder_1_out0[19]),
    .out20(decoder_1_out0[20]), .out21(decoder_1_out0[21]), .out22(decoder_1_out0[22]),
    .out23(decoder_1_out0[23]), .out24(decoder_1_out0[24]), .out25(decoder_1_out0[25]),
    .out26(decoder_1_out0[26]), .out27(decoder_1_out0[27]), .out28(decoder_1_out0[28]),
    .out29(decoder_1_out0[29]), .out30(decoder_1_out0[30]), .out31(decoder_1_out0[31]), .sel(not_8_out),
    .en(not_1_out));
  Decoder #(.select(5)) decoder_2 (
    .out0(decoder_2_out0[0]), .out1(decoder_2_out0[1]), .out2(decoder_2_out0[2]), .out3(decoder_2_out0[3]),
    .out4(decoder_2_out0[4]), .out5(decoder_2_out0[5]), .out6(decoder_2_out0[6]), .out7(decoder_2_out0[7]),
    .out8(decoder_2_out0[8]), .out9(decoder_2_out0[9]), .out10(decoder_2_out0[10]),
    .out11(decoder_2_out0[11]), .out12(decoder_2_out0[12]), .out13(decoder_2_out0[13]),
    .out14(decoder_2_out0[14]), .out15(decoder_2_out0[15]), .out16(decoder_2_out0[16]),
    .out17(decoder_2_out0[17]), .out18(decoder_2_out0[18]), .out19(decoder_2_out0[19]),
    .out20(decoder_2_out0[20]), .out21(decoder_2_out0[21]), .out22(decoder_2_out0[22]),
    .out23(decoder_2_out0[23]), .out24(decoder_2_out0[24]), .out25(decoder_2_out0[25]),
    .out26(decoder_2_out0[26]), .out27(decoder_2_out0[27]), .out28(decoder_2_out0[28]),
    .out29(decoder_2_out0[29]), .out30(decoder_2_out0[30]), .out31(decoder_2_out0[31]), .sel(random_1_out),
    .en(not_1_out));
  Clock clock_3 (.out(clock_3_out));
  and and_8 (and_8_out, clock_3_out, or_1_out);
  Random #(.width(5), .seed(1504)) random_2 (.clk(and_8_out), .out(random_2_out));  // open: next, clr
  Demultiplexer #(.select(5), .width(32)) demultiplexer_1 (
    .out0(demultiplexer_1_out0), .out1(demultiplexer_1_out1), .out2(demultiplexer_1_out2),
    .out3(demultiplexer_1_out3), .out4(demultiplexer_1_out4), .out5(demultiplexer_1_out5),
    .out6(demultiplexer_1_out6), .out7(demultiplexer_1_out7), .out8(demultiplexer_1_out8),
    .out9(demultiplexer_1_out9), .out10(demultiplexer_1_out10), .out11(demultiplexer_1_out11),
    .out12(demultiplexer_1_out12), .out13(demultiplexer_1_out13), .out14(demultiplexer_1_out14),
    .out15(demultiplexer_1_out15), .out16(demultiplexer_1_out16), .out17(demultiplexer_1_out17),
    .out18(demultiplexer_1_out18), .out19(demultiplexer_1_out19), .out20(demultiplexer_1_out20),
    .out21(demultiplexer_1_out21), .out22(demultiplexer_1_out22), .out23(demultiplexer_1_out23),
    .out24(demultiplexer_1_out24), .out25(demultiplexer_1_out25), .out26(demultiplexer_1_out26),
    .out27(demultiplexer_1_out27), .out28(demultiplexer_1_out28), .out29(demultiplexer_1_out29),
    .out30(demultiplexer_1_out30), .out31(demultiplexer_1_out31), .in(decoder_1_out0), .sel(counter_2_q),
    .en(not_1_out));
  Demultiplexer #(.select(5), .width(32)) demultiplexer_2 (
    .out0(demultiplexer_2_out0), .out1(demultiplexer_2_out1), .out2(demultiplexer_2_out2),
    .out3(demultiplexer_2_out3), .out4(demultiplexer_2_out4), .out5(demultiplexer_2_out5),
    .out6(demultiplexer_2_out6), .out7(demultiplexer_2_out7), .out8(demultiplexer_2_out8),
    .out9(demultiplexer_2_out9), .out10(demultiplexer_2_out10), .out11(demultiplexer_2_out11),
    .out12(demultiplexer_2_out12), .out13(demultiplexer_2_out13), .out14(demultiplexer_2_out14),
    .out15(demultiplexer_2_out15), .out16(demultiplexer_2_out16), .out17(demultiplexer_2_out17),
    .out18(demultiplexer_2_out18), .out19(demultiplexer_2_out19), .out20(demultiplexer_2_out20),
    .out21(demultiplexer_2_out21), .out22(demultiplexer_2_out22), .out23(demultiplexer_2_out23),
    .out24(demultiplexer_2_out24), .out25(demultiplexer_2_out25), .out26(demultiplexer_2_out26),
    .out27(demultiplexer_2_out27), .out28(demultiplexer_2_out28), .out29(demultiplexer_2_out29),
    .out30(demultiplexer_2_out30), .out31(demultiplexer_2_out31), .in(decoder_2_out0), .sel(random_2_out),
    .en(not_1_out));
  Joystick #(.bits(2)) joystick_1 (.x(joystick_1_x), .y(joystick_1_y));
  DotMatrix #(.matrixcols(32), .matrixrows(32)) dotmatrix_1 (
    .col0(comparador_1_s1), .col1(comparador_1_s2), .col2(comparador_1_s3), .col3(comparador_1_s4),
    .col4(comparador_1_s5), .col5(comparador_1_s6), .col6(comparador_1_s7), .col7(comparador_1_s8),
    .col8(comparador_1_s9), .col9(comparador_1_s10), .col10(comparador_1_s11), .col11(comparador_1_s12),
    .col12(comparador_1_s13), .col13(comparador_1_s14), .col14(comparador_1_s15), .col15(comparador_1_s16),
    .col16(comparador_1_s17), .col17(comparador_1_s18), .col18(comparador_1_s19), .col19(comparador_1_s20),
    .col20(comparador_1_s21), .col21(comparador_1_s22), .col22(comparador_1_s23), .col23(comparador_1_s24),
    .col24(comparador_1_s25), .col25(comparador_1_s26), .col26(comparador_1_s27), .col27(comparador_1_s28),
    .col28(comparador_1_s29), .col29(comparador_1_s30), .col30(comparador_1_s31), .col31(comparador_1_s32));
  comparador comparador_1 (
    .in_1(demultiplexer_1_out0), .in_2(demultiplexer_2_out0), .in_3(demultiplexer_1_out1),
    .in_4(demultiplexer_2_out1), .in_5(demultiplexer_1_out2), .in_6(demultiplexer_2_out2),
    .in_7(demultiplexer_1_out3), .in_8(demultiplexer_2_out3), .in_9(demultiplexer_1_out4),
    .in_10(demultiplexer_2_out4), .in_11(demultiplexer_1_out5), .in_12(demultiplexer_2_out5),
    .in_13(demultiplexer_1_out6), .in_14(demultiplexer_2_out6), .in_15(demultiplexer_1_out7),
    .in_16(demultiplexer_2_out7), .in_17(demultiplexer_1_out8), .in_18(demultiplexer_2_out8),
    .in_19(demultiplexer_1_out9), .in_20(demultiplexer_2_out9), .in_21(demultiplexer_1_out10),
    .in_22(demultiplexer_2_out10), .in_23(demultiplexer_1_out11), .in_24(demultiplexer_2_out11),
    .in_25(demultiplexer_1_out12), .in_26(demultiplexer_2_out12), .in_27(demultiplexer_1_out13),
    .in_28(demultiplexer_2_out13), .in_29(demultiplexer_1_out14), .in_30(demultiplexer_2_out14),
    .in_31(demultiplexer_1_out15), .in_32(demultiplexer_2_out15), .in_33(demultiplexer_1_out16),
    .in_34(demultiplexer_2_out16), .in_35(demultiplexer_1_out17), .in_36(demultiplexer_2_out17),
    .in_37(demultiplexer_1_out18), .in_38(demultiplexer_2_out18), .in_39(demultiplexer_1_out19),
    .in_40(demultiplexer_2_out19), .in_41(demultiplexer_1_out20), .in_42(demultiplexer_2_out20),
    .in_43(demultiplexer_1_out21), .in_44(demultiplexer_2_out21), .in_45(demultiplexer_1_out22),
    .in_46(demultiplexer_2_out22), .in_47(demultiplexer_1_out23), .in_48(demultiplexer_2_out23),
    .in_49(demultiplexer_1_out24), .in_50(demultiplexer_2_out24), .in_51(demultiplexer_1_out25),
    .in_52(demultiplexer_2_out25), .in_53(demultiplexer_1_out26), .in_54(demultiplexer_2_out26),
    .in_55(demultiplexer_1_out27), .in_56(demultiplexer_2_out27), .in_57(demultiplexer_1_out28),
    .in_58(demultiplexer_2_out28), .in_59(demultiplexer_1_out29), .in_60(demultiplexer_2_out29),
    .in_61(demultiplexer_1_out30), .in_62(demultiplexer_2_out30), .in_63(demultiplexer_1_out31),
    .in_64(demultiplexer_2_out31), .sc1(comparador_1_sc1), .s1(comparador_1_s1), .sc2(comparador_1_sc2),
    .s2(comparador_1_s2), .sc3(comparador_1_sc3), .s3(comparador_1_s3), .sc4(comparador_1_sc4),
    .s4(comparador_1_s4), .sc5(comparador_1_sc5), .s5(comparador_1_s5), .sc6(comparador_1_sc6),
    .s6(comparador_1_s6), .sc7(comparador_1_sc7), .s7(comparador_1_s7), .sc8(comparador_1_sc8),
    .s8(comparador_1_s8), .sc9(comparador_1_sc9), .s9(comparador_1_s9), .sc10(comparador_1_sc10),
    .s10(comparador_1_s10), .sc11(comparador_1_sc11), .s11(comparador_1_s11), .sc12(comparador_1_sc12),
    .s12(comparador_1_s12), .sc13(comparador_1_sc13), .s13(comparador_1_s13), .sc14(comparador_1_sc14),
    .s14(comparador_1_s14), .sc15(comparador_1_sc15), .s15(comparador_1_s15), .sc16(comparador_1_sc16),
    .s16(comparador_1_s16), .sc17(comparador_1_sc17), .s17(comparador_1_s17), .sc18(comparador_1_sc18),
    .s18(comparador_1_s18), .sc19(comparador_1_sc19), .s19(comparador_1_s19), .sc20(comparador_1_sc20),
    .s20(comparador_1_s20), .sc21(comparador_1_sc21), .s21(comparador_1_s21), .sc22(comparador_1_sc22),
    .s22(comparador_1_s22), .sc23(comparador_1_sc23), .s23(comparador_1_s23), .sc24(comparador_1_sc24),
    .s24(comparador_1_s24), .sc25(comparador_1_sc25), .s25(comparador_1_s25), .sc26(comparador_1_sc26),
    .s26(comparador_1_s26), .sc27(comparador_1_sc27), .s27(comparador_1_s27), .sc28(comparador_1_sc28),
    .s28(comparador_1_s28), .sc29(comparador_1_sc29), .s29(comparador_1_s29), .sc30(comparador_1_sc30),
    .s30(comparador_1_s30), .sc31(comparador_1_sc31), .s31(comparador_1_s31), .sc32(comparador_1_sc32),
    .s32(comparador_1_s32));
  or or_1 (or_1_out, comparador_1_sc2, comparador_1_sc3, comparador_1_sc4, comparador_1_sc5, comparador_1_sc6, comparador_1_sc7, comparador_1_sc8, comparador_1_sc9, comparador_1_sc10, comparador_1_sc11, comparador_1_sc12, comparador_1_sc13, comparador_1_sc14, comparador_1_sc15, comparador_1_sc16, comparador_1_sc17, comparador_1_sc18, comparador_1_sc19, comparador_1_sc20, comparador_1_sc21, comparador_1_sc22, comparador_1_sc23, comparador_1_sc24, comparador_1_sc25, comparador_1_sc26, comparador_1_sc27, comparador_1_sc28, comparador_1_sc29, comparador_1_sc30, comparador_1_sc31, comparador_1_sc32, comparador_1_sc1);
  Counter #(.width(10), .max('h3ff)) counter_3 (.clk(or_1_out));  // open: load, D, count, Q, carry, clr
endmodule

module comparador (
  input  [31:0] in_1,
  input  [31:0] in_2,
  input  [31:0] in_3,
  input  [31:0] in_4,
  input  [31:0] in_5,
  input  [31:0] in_6,
  input  [31:0] in_7,
  input  [31:0] in_8,
  input  [31:0] in_9,
  input  [31:0] in_10,
  input  [31:0] in_11,
  input  [31:0] in_12,
  input  [31:0] in_13,
  input  [31:0] in_14,
  input  [31:0] in_15,
  input  [31:0] in_16,
  input  [31:0] in_17,
  input  [31:0] in_18,
  input  [31:0] in_19,
  input  [31:0] in_20,
  input  [31:0] in_21,
  input  [31:0] in_22,
  input  [31:0] in_23,
  input  [31:0] in_24,
  input  [31:0] in_25,
  input  [31:0] in_26,
  input  [31:0] in_27,
  input  [31:0] in_28,
  input  [31:0] in_29,
  input  [31:0] in_30,
  input  [31:0] in_31,
  input  [31:0] in_32,
  input  [31:0] in_33,
  input  [31:0] in_34,
  input  [31:0] in_35,
  input  [31:0] in_36,
  input  [31:0] in_37,
  input  [31:0] in_38,
  input  [31:0] in_39,
  input  [31:0] in_40,
  input  [31:0] in_41,
  input  [31:0] in_42,
  input  [31:0] in_43,
  input  [31:0] in_44,
  input  [31:0] in_45,
  input  [31:0] in_46,
  input  [31:0] in_47,
  input  [31:0] in_48,
  input  [31:0] in_49,
  input  [31:0] in_50,
  input  [31:0] in_51,
  input  [31:0] in_52,
  input  [31:0] in_53,
  input  [31:0] in_54,
  input  [31:0] in_55,
  input  [31:0] in_56,
  input  [31:0] in_57,
  input  [31:0] in_58,
  input  [31:0] in_59,
  input  [31:0] in_60,
  input  [31:0] in_61,
  input  [31:0] in_62,
  input  [31:0] in_63,
  input  [31:0] in_64,
  output sc1,
  output [31:0] s1,
  output sc2,
  output [31:0] s2,
  output sc3,
  output [31:0] s3,
  output sc4,
  output [31:0] s4,
  output sc5,
  output [31:0] s5,
  output sc6,
  output [31:0] s6,
  output sc7,
  output [31:0] s7,
  output sc8,
  output [31:0] s8,
  output sc9,
  output [31:0] s9,
  output sc10,
  output [31:0] s10,
  output sc11,
  output [31:0] s11,
  output sc12,
  output [31:0] s12,
  output sc13,
  output [31:0] s13,
  output sc14,
  output [31:0] s14,
  output sc15,
  output [31:0] s15,
  output sc16,
  output [31:0] s16,
  output sc17,
  output [31:0] s17,
  output sc18,
  output [31:0] s18,
  output sc19,
  output [31:0] s19,
  output sc20,
  output [31:0] s20,
  output sc21,
  output [31:0] s21,
  output sc22,
  output [31:0] s22,
  output sc23,
  output [31:0] s23,
  output sc24,
  output [31:0] s24,
  output sc25,
  output [31:0] s25,
  output sc26,
  output [31:0] s26,
  output sc27,
  output [31:0] s27,
  output sc28,
  output [31:0] s28,
  output sc29,
  output [31:0] s29,
  output sc30,
  output [31:0] s30,
  output sc31,
  output [31:0] s31,
  output sc32,
  output [31:0] s32
);

  wire comparator_1_eq, comparator_2_eq, comparator_3_eq, comparator_4_eq, comparator_5_eq, comparator_6_eq,
       comparator_7_eq, comparator_8_eq, comparator_9_eq, comparator_10_eq, comparator_11_eq,
       comparator_12_eq, comparator_13_eq, comparator_14_eq, comparator_15_eq, comparator_16_eq,
       comparator_17_eq, comparator_18_eq, comparator_19_eq, comparator_20_eq, comparator_21_eq,
       comparator_22_eq, comparator_23_eq, comparator_24_eq, comparator_25_eq, comparator_26_eq,
       comparator_27_eq, comparator_28_eq, comparator_29_eq, comparator_30_eq, comparator_31_eq,
       comparator_32_eq, comparator_32_gt, not_1_out, not_2_out, not_3_out, not_4_out, not_5_out, not_6_out,
       not_7_out, not_8_out, not_9_out, not_10_out, not_11_out, not_12_out, not_13_out, not_14_out,
       not_15_out, not_16_out, not_17_out, not_18_out, not_19_out, not_20_out, not_21_out, not_22_out,
       not_23_out, not_24_out, not_25_out, not_26_out, not_27_out, not_28_out, not_29_out, not_30_out,
       not_31_out, not_32_out, not_33_out, not_34_out, not_35_out, not_36_out, not_37_out, not_38_out,
       not_39_out, not_40_out, not_41_out, not_42_out, not_43_out, not_44_out, not_45_out, not_46_out,
       not_47_out, not_48_out, not_49_out, not_50_out, not_51_out, not_52_out, not_53_out, not_54_out,
       not_55_out, not_56_out, not_57_out, not_58_out, not_59_out, not_60_out, not_61_out, not_62_out,
       not_63_out, not_64_out;
  wire [31:0] controlled_buffer_1_out, controlled_buffer_2_out, controlled_buffer_3_out,
       controlled_buffer_4_out, controlled_buffer_5_out, controlled_buffer_6_out, controlled_buffer_7_out,
       controlled_buffer_8_out, controlled_buffer_9_out, controlled_buffer_10_out, controlled_buffer_11_out,
       controlled_buffer_12_out, controlled_buffer_13_out, controlled_buffer_14_out,
       controlled_buffer_15_out, controlled_buffer_16_out, controlled_buffer_17_out,
       controlled_buffer_18_out, controlled_buffer_19_out, controlled_buffer_20_out,
       controlled_buffer_21_out, controlled_buffer_22_out, controlled_buffer_23_out,
       controlled_buffer_24_out, controlled_buffer_25_out, controlled_buffer_26_out,
       controlled_buffer_27_out, controlled_buffer_28_out, controlled_buffer_29_out,
       controlled_buffer_30_out, controlled_buffer_31_out, controlled_buffer_32_out,
       controlled_buffer_33_out, controlled_buffer_34_out, controlled_buffer_35_out,
       controlled_buffer_36_out, controlled_buffer_37_out, controlled_buffer_38_out,
       controlled_buffer_39_out, controlled_buffer_40_out, controlled_buffer_41_out,
       controlled_buffer_42_out, controlled_buffer_43_out, controlled_buffer_44_out,
       controlled_buffer_45_out, controlled_buffer_46_out, controlled_buffer_47_out,
       controlled_buffer_48_out, controlled_buffer_49_out, controlled_buffer_50_out,
       controlled_buffer_51_out, controlled_buffer_52_out, controlled_buffer_53_out,
       controlled_buffer_54_out, controlled_buffer_55_out, controlled_buffer_56_out,
       controlled_buffer_57_out, controlled_buffer_58_out, controlled_buffer_59_out,
       controlled_buffer_60_out, controlled_buffer_61_out, controlled_buffer_62_out,
       controlled_buffer_63_out, controlled_buffer_64_out;

  distro distro_1 (.in_1(in_59), .in_2(in_60), .out_3(sc30));
  distro distro_2 (.in_1(in_63), .in_2(in_64), .out_3(sc32));
  distro distro_3 (.in_1(in_1), .in_2(in_2), .out_3(sc1));
  distro distro_4 (.in_1(in_3), .in_2(in_4), .out_3(sc2));
  assign controlled_buffer_1_out = not_1_out ? in_3 : 32'bz;  // Controlled_Buffer controlled_buffer_1
  not not_1 (not_1_out, comparator_1_eq);
  Comparator #(.width(32)) comparator_1 (.a(in_3), .b(in_4), .eq(comparator_1_eq));  // open: gt, lt
  not not_2 (not_2_out, comparator_1_eq);
  assign controlled_buffer_2_out = not_2_out ? in_4 : 32'bz;  // Controlled_Buffer controlled_buffer_2
  distro distro_5 (.in_1(in_5), .in_2(in_6), .out_3(sc3));
  assign controlled_buffer_3_out = not_3_out ? in_5 : 32'bz;  // Controlled_Buffer controlled_buffer_3
  not not_3 (not_3_out, comparator_2_eq);
  Comparator #(.width(32)) comparator_2 (.a(in_5), .b(in_6), .eq(comparator_2_eq));  // open: gt, lt
  not not_4 (not_4_out, comparator_2_eq);
  assign controlled_buffer_4_out = not_4_out ? in_6 : 32'bz;  // Controlled_Buffer controlled_buffer_4
  distro distro_6 (.in_1(in_7), .in_2(in_8), .out_3(sc4));
  assign controlled_buffer_5_out = not_5_out ? in_7 : 32'bz;  // Controlled_Buffer controlled_buffer_5
  not not_5 (not_5_out, comparator_3_eq);
  Comparator #(.width(32)) comparator_3 (.a(in_7), .b(in_8), .eq(comparator_3_eq));  // open: gt, lt
  not not_6 (not_6_out, comparator_3_eq);
  assign controlled_buffer_6_out = not_6_out ? in_8 : 32'bz;  // Controlled_Buffer controlled_buffer_6
  distro distro_7 (.in_1(in_9), .in_2(in_10), .out_3(sc5));
  assign controlled_buffer_7_out = not_7_out ? in_9 : 32'bz;  // Controlled_Buffer controlled_buffer_7
  not not_7 (not_7_out, comparator_4_eq);
  Comparator #(.width(32)) comparator_4 (.a(in_9), .b(in_10), .eq(comparator_4_eq));  // open: gt, lt
  not not_8 (not_8_out, comparator_4_eq);
  assign controlled_buffer_8_out = not_8_out ? in_10 : 32'bz;  // Controlled_Buffer controlled_buffer_8
  distro distro_8 (.in_1(in_11), .in_2(in_12), .out_3(sc6));
  assign controlled_buffer_9_out = not_9_out ? in_11 : 32'bz;  // Controlled_Buffer controlled_buffer_9
  not not_9 (not_9_out, comparator_5_eq);
  Comparator #(.width(32)) comparator_5 (.a(in_11), .b(in_12), .eq(comparator_5_eq));  // open: gt, lt
  not not_10 (not_10_out, comparator_5_eq);
  assign controlled_buffer_10_out = not_10_out ? in_12 : 32'bz;  // Controlled_Buffer controlled_buffer_10
  distro distro_9 (.in_1(in_13), .in_2(in_14), .out_3(sc7));
  assign controlled_buffer_11_out = not_11_out ? in_13 : 32'bz;  // Controlled_Buffer controlled_buffer_11
  not not_11 (not_11_out, comparator_6_eq);
  Comparator #(.width(32)) comparator_6 (.a(in_13), .b(in_14), .eq(comparator_6_eq));  // open: gt, lt
  not not_12 (not_12_out, comparator_6_eq);
  assign controlled_buffer_12_out = not_12_out ? in_14 : 32'bz;  // Controlled_Buffer controlled_buffer_12
  distro distro_10 (.in_1(in_15), .in_2(in_16), .out_3(sc8));
  assign controlled_buffer_13_out = not_13_out ? in_15 : 32'bz;  // Controlled_Buffer controlled_buffer_13
  not not_13 (not_13_out, comparator_7_eq);
  Comparator #(.width(32)) comparator_7 (.a(in_15), .b(in_16), .eq(comparator_7_eq));  // open: gt, lt
  not not_14 (not_14_out, comparator_7_eq);
  assign controlled_buffer_14_out = not_14_out ? in_16 : 32'bz;  // Controlled_Buffer controlled_buffer_14
  distro distro_11 (.in_1(in_17), .in_2(in_18), .out_3(sc9));
  assign controlled_buffer_15_out = not_15_out ? in_17 : 32'bz;  // Controlled_Buffer controlled_buffer_15
  not not_15 (not_15_out, comparator_8_eq);
  Comparator #(.width(32)) comparator_8 (.a(in_17), .b(in_18), .eq(comparator_8_eq));  // open: gt, lt
  not not_16 (not_16_out, comparator_8_eq);
  assign controlled_buffer_16_out = not_16_out ? in_18 : 32'bz;  // Controlled_Buffer controlled_buffer_16
  distro distro_12 (.in_1(in_19), .in_2(in_20), .out_3(sc10));
  assign controlled_buffer_17_out = not_17_out ? in_19 : 32'bz;  // Controlled_Buffer controlled_buffer_17
  not not_17 (not_17_out, comparator_9_eq);
  Comparator #(.width(32)) comparator_9 (.a(in_19), .b(in_20), .eq(comparator_9_eq));  // open: gt, lt
  not not_18 (not_18_out, comparator_9_eq);
  assign controlled_buffer_18_out = not_18_out ? in_20 : 32'bz;  // Controlled_Buffer controlled_buffer_18
  distro distro_13 (.in_1(in_21), .in_2(in_22), .out_3(sc11));
  assign controlled_buffer_19_out = not_19_out ? in_21 : 32'bz;  // Controlled_Buffer controlled_buffer_19
  not not_19 (not_19_out, comparator_10_eq);
  Comparator #(.width(32)) comparator_10 (.a(in_21), .b(in_22), .eq(comparator_10_eq));  // open: gt, lt
  not not_20 (not_20_out, comparator_10_eq);
  assign controlled_buffer_20_out = not_20_out ? in_22 : 32'bz;  // Controlled_Buffer controlled_buffer_20
  distro distro_14 (.in_1(in_23), .in_2(in_24), .out_3(sc12));
  assign controlled_buffer_21_out = not_21_out ? in_23 : 32'bz;  // Controlled_Buffer controlled_buffer_21
  not not_21 (not_21_out, comparator_11_eq);
  Comparator #(.width(32)) comparator_11 (.a(in_23), .b(in_24), .eq(comparator_11_eq));  // open: gt, lt
  not not_22 (not_22_out, comparator_11_eq);
  assign controlled_buffer_22_out = not_22_out ? in_24 : 32'bz;  // Controlled_Buffer controlled_buffer_22
  distro distro_15 (.in_1(in_25), .in_2(in_26), .out_3(sc13));
  assign controlled_buffer_23_out = not_23_out ? in_25 : 32'bz;  // Controlled_Buffer controlled_buffer_23
  not not_23 (not_23_out, comparator_12_eq);
  Comparator #(.width(32)) comparator_12 (.a(in_25), .b(in_26), .eq(comparator_12_eq));  // open: gt, lt
  not not_24 (not_24_out, comparator_12_eq);
  assign controlled_buffer_24_out = not_24_out ? in_26 : 32'bz;  // Controlled_Buffer controlled_buffer_24
  distro distro_16 (.in_1(in_27), .in_2(in_28), .out_3(sc14));
  assign controlled_buffer_25_out = not_25_out ? in_27 : 32'bz;  // Controlled_Buffer controlled_buffer_25
  not not_25 (not_25_out, comparator_13_eq);
  Comparator #(.width(32)) comparator_13 (.a(in_27), .b(in_28), .eq(comparator_13_eq));  // open: gt, lt
  not not_26 (not_26_out, comparator_13_eq);
  assign controlled_buffer_26_out = not_26_out ? in_28 : 32'bz;  // Controlled_Buffer controlled_buffer_26
  distro distro_17 (.in_1(in_29), .in_2(in_30), .out_3(sc15));
  assign controlled_buffer_27_out = not_27_out ? in_29 : 32'bz;  // Controlled_Buffer controlled_buffer_27
  not not_27 (not_27_out, comparator_14_eq);
  Comparator #(.width(32)) comparator_14 (.a(in_29), .b(in_30), .eq(comparator_14_eq));  // open: gt, lt
  not not_28 (not_28_out, comparator_14_eq);
  assign controlled_buffer_28_out = not_28_out ? in_30 : 32'bz;  // Controlled_Buffer controlled_buffer_28
  distro distro_18 (.in_1(in_31), .in_2(in_32), .out_3(sc16));
  assign controlled_buffer_29_out = not_29_out ? in_31 : 32'bz;  // Controlled_Buffer controlled_buffer_29
  not not_29 (not_29_out, comparator_15_eq);
  Comparator #(.width(32)) comparator_15 (.a(in_31), .b(in_32), .eq(comparator_15_eq));  // open: gt, lt
  not not_30 (not_30_out, comparator_15_eq);
  assign controlled_buffer_30_out = not_30_out ? in_32 : 32'bz;  // Controlled_Buffer controlled_buffer_30
  distro distro_19 (.in_1(in_33), .in_2(in_34), .out_3(sc17));
  assign controlled_buffer_31_out = not_31_out ? in_33 : 32'bz;  // Controlled_Buffer controlled_buffer_31
  not not_31 (not_31_out, comparator_16_eq);
  Comparator #(.width(32)) comparator_16 (.a(in_33), .b(in_34), .eq(comparator_16_eq));  // open: gt, lt
  not not_32 (not_32_out, comparator_16_eq);
  assign controlled_buffer_32_out = not_32_out ? in_34 : 32'bz;  // Controlled_Buffer controlled_buffer_32
  distro distro_20 (.in_1(in_35), .in_2(in_36), .out_3(sc18));
  assign controlled_buffer_33_out = not_33_out ? in_35 : 32'bz;  // Controlled_Buffer controlled_buffer_33
  not not_33 (not_33_out, comparator_17_eq);
  Comparator #(.width(32)) comparator_17 (.a(in_35), .b(in_36), .eq(comparator_17_eq));  // open: gt, lt
  not not_34 (not_34_out, comparator_17_eq);
  assign controlled_buffer_34_out = not_34_out ? in_36 : 32'bz;  // Controlled_Buffer controlled_buffer_34
  distro distro_21 (.in_1(in_37), .in_2(in_38), .out_3(sc19));
  assign controlled_buffer_35_out = not_35_out ? in_37 : 32'bz;  // Controlled_Buffer controlled_buffer_35
  not not_35 (not_35_out, comparator_18_eq);
  Comparator #(.width(32)) comparator_18 (.a(in_37), .b(in_38), .eq(comparator_18_eq));  // open: gt, lt
  not not_36 (not_36_out, comparator_18_eq);
  assign controlled_buffer_36_out = not_36_out ? in_38 : 32'bz;  // Controlled_Buffer controlled_buffer_36
  distro distro_22 (.in_1(in_39), .in_2(in_40), .out_3(sc20));
  assign controlled_buffer_37_out = not_37_out ? in_39 : 32'bz;  // Controlled_Buffer controlled_buffer_37
  not not_37 (not_37_out, comparator_19_eq);
  Comparator #(.width(32)) comparator_19 (.a(in_39), .b(in_40), .eq(comparator_19_eq));  // open: gt, lt
  not not_38 (not_38_out, comparator_19_eq);
  assign controlled_buffer_38_out = not_38_out ? in_40 : 32'bz;  // Controlled_Buffer controlled_buffer_38
  distro distro_23 (.in_1(in_41), .in_2(in_42), .out_3(sc21));
  assign controlled_buffer_39_out = not_39_out ? in_41 : 32'bz;  // Controlled_Buffer controlled_buffer_39
  not not_39 (not_39_out, comparator_20_eq);
  Comparator #(.width(32)) comparator_20 (.a(in_41), .b(in_42), .eq(comparator_20_eq));  // open: gt, lt
  not not_40 (not_40_out, comparator_20_eq);
  assign controlled_buffer_40_out = not_40_out ? in_42 : 32'bz;  // Controlled_Buffer controlled_buffer_40
  distro distro_24 (.in_1(in_43), .in_2(in_44), .out_3(sc22));
  assign controlled_buffer_41_out = not_41_out ? in_43 : 32'bz;  // Controlled_Buffer controlled_buffer_41
  not not_41 (not_41_out, comparator_21_eq);
  Comparator #(.width(32)) comparator_21 (.a(in_43), .b(in_44), .eq(comparator_21_eq));  // open: gt, lt
  not not_42 (not_42_out, comparator_21_eq);
  assign controlled_buffer_42_out = not_42_out ? in_44 : 32'bz;  // Controlled_Buffer controlled_buffer_42
  distro distro_25 (.in_1(in_45), .in_2(in_46), .out_3(sc23));
  assign controlled_buffer_43_out = not_43_out ? in_45 : 32'bz;  // Controlled_Buffer controlled_buffer_43
  not not_43 (not_43_out, comparator_22_eq);
  Comparator #(.width(32)) comparator_22 (.a(in_45), .b(in_46), .eq(comparator_22_eq));  // open: gt, lt
  not not_44 (not_44_out, comparator_22_eq);
  assign controlled_buffer_44_out = not_44_out ? in_46 : 32'bz;  // Controlled_Buffer controlled_buffer_44
  distro distro_26 (.in_1(in_47), .in_2(in_48), .out_3(sc24));
  assign controlled_buffer_45_out = not_45_out ? in_47 : 32'bz;  // Controlled_Buffer controlled_buffer_45
  not not_45 (not_45_out, comparator_23_eq);
  Comparator #(.width(32)) comparator_23 (.a(in_47), .b(in_48), .eq(comparator_23_eq));  // open: gt, lt
  not not_46 (not_46_out, comparator_23_eq);
  assign controlled_buffer_46_out = not_46_out ? in_48 : 32'bz;  // Controlled_Buffer controlled_buffer_46
  distro distro_27 (.in_1(in_49), .in_2(in_50), .out_3(sc25));
  assign controlled_buffer_47_out = not_47_out ? in_49 : 32'bz;  // Controlled_Buffer controlled_buffer_47
  not not_47 (not_47_out, comparator_24_eq);
  Comparator #(.width(32)) comparator_24 (.a(in_49), .b(in_50), .eq(comparator_24_eq));  // open: gt, lt
  not not_48 (not_48_out, comparator_24_eq);
  assign controlled_buffer_48_out = not_48_out ? in_50 : 32'bz;  // Controlled_Buffer controlled_buffer_48
  distro distro_28 (.in_1(in_51), .in_2(in_52), .out_3(sc26));
  assign controlled_buffer_49_out = not_49_out ? in_51 : 32'bz;  // Controlled_Buffer controlled_buffer_49
  not not_49 (not_49_out, comparator_25_eq);
  Comparator #(.width(32)) comparator_25 (.a(in_51), .b(in_52), .eq(comparator_25_eq));  // open: gt, lt
  not not_50 (not_50_out, comparator_25_eq);
  assign controlled_buffer_50_out = not_50_out ? in_52 : 32'bz;  // Controlled_Buffer controlled_buffer_50
  distro distro_29 (.in_1(in_53), .in_2(in_54), .out_3(sc27));
  assign controlled_buffer_51_out = not_51_out ? in_53 : 32'bz;  // Controlled_Buffer controlled_buffer_51
  not not_51 (not_51_out, comparator_26_eq);
  Comparator #(.width(32)) comparator_26 (.a(in_53), .b(in_54), .eq(comparator_26_eq));  // open: gt, lt
  not not_52 (not_52_out, comparator_26_eq);
  assign controlled_buffer_52_out = not_52_out ? in_54 : 32'bz;  // Controlled_Buffer controlled_buffer_52
  distro distro_30 (.in_1(in_55), .in_2(in_56), .out_3(sc28));
  assign controlled_buffer_53_out = not_53_out ? in_55 : 32'bz;  // Controlled_Buffer controlled_buffer_53
  not not_53 (not_53_out, comparator_27_eq);
  Comparator #(.width(32)) comparator_27 (.a(in_55), .b(in_56), .eq(comparator_27_eq));  // open: gt, lt
  not not_54 (not_54_out, comparator_27_eq);
  assign controlled_buffer_54_out = not_54_out ? in_56 : 32'bz;  // Controlled_Buffer controlled_buffer_54
  distro distro_31 (.in_1(in_57), .in_2(in_58), .out_3(sc29));
  assign controlled_buffer_55_out = not_55_out ? in_57 : 32'bz;  // Controlled_Buffer controlled_buffer_55
  not not_55 (not_55_out, comparator_28_eq);
  Comparator #(.width(32)) comparator_28 (.a(in_57), .b(in_58), .eq(comparator_28_eq));  // open: gt, lt
  not not_56 (not_56_out, comparator_28_eq);
  assign controlled_buffer_56_out = not_56_out ? in_58 : 32'bz;  // Controlled_Buffer controlled_buffer_56
  assign controlled_buffer_57_out = not_57_out ? in_59 : 32'bz;  // Controlled_Buffer controlled_buffer_57
  not not_57 (not_57_out, comparator_29_eq);
  Comparator #(.width(32)) comparator_29 (.a(in_59), .b(in_60), .eq(comparator_29_eq));  // open: gt, lt
  not not_58 (not_58_out, comparator_29_eq);
  assign controlled_buffer_58_out = not_58_out ? in_60 : 32'bz;  // Controlled_Buffer controlled_buffer_58
  distro distro_32 (.in_1(in_61), .in_2(in_62), .out_3(sc31));
  assign controlled_buffer_59_out = not_59_out ? in_61 : 32'bz;  // Controlled_Buffer controlled_buffer_59
  not not_59 (not_59_out, comparator_30_eq);
  Comparator #(.width(32)) comparator_30 (.a(in_61), .b(in_62), .eq(comparator_30_eq));  // open: gt, lt
  not not_60 (not_60_out, comparator_30_eq);
  assign controlled_buffer_60_out = not_60_out ? in_62 : 32'bz;  // Controlled_Buffer controlled_buffer_60
  assign controlled_buffer_61_out = not_61_out ? in_63 : 32'bz;  // Controlled_Buffer controlled_buffer_61
  not not_61 (not_61_out, comparator_31_eq);
  Comparator #(.width(32)) comparator_31 (.a(in_63), .b(in_64), .eq(comparator_31_eq));  // open: gt, lt
  not not_62 (not_62_out, comparator_31_eq);
  assign controlled_buffer_62_out = not_62_out ? in_64 : 32'bz;  // Controlled_Buffer controlled_buffer_62
  assign controlled_buffer_63_out = not_63_out ? in_1 : 32'bz;  // Controlled_Buffer controlled_buffer_63
  not not_63 (not_63_out, comparator_32_gt);
  Comparator #(.width(32)) comparator_32 (
    .a(in_1), .b(in_2), .gt(comparator_32_gt), .eq(comparator_32_eq));  // open: lt
  not not_64 (not_64_out, comparator_32_eq);
  assign controlled_buffer_64_out = not_64_out ? in_2 : 32'bz;  // Controlled_Buffer controlled_buffer_64
  assign s2 = comparator_1_eq ? in_3 : 32'bz;  // Controlled_Buffer controlled_buffer_65
  assign s3 = comparator_2_eq ? in_5 : 32'bz;  // Controlled_Buffer controlled_buffer_66
  assign s4 = comparator_3_eq ? in_7 : 32'bz;  // Controlled_Buffer controlled_buffer_67
  assign s5 = comparator_4_eq ? in_9 : 32'bz;  // Controlled_Buffer controlled_buffer_68
  assign s6 = comparator_5_eq ? in_11 : 32'bz;  // Controlled_Buffer controlled_buffer_69
  assign s7 = comparator_6_eq ? in_13 : 32'bz;  // Controlled_Buffer controlled_buffer_70
  assign s8 = comparator_7_eq ? in_15 : 32'bz;  // Controlled_Buffer controlled_buffer_71
  assign s9 = comparator_8_eq ? in_17 : 32'bz;  // Controlled_Buffer controlled_buffer_72
  assign s10 = comparator_9_eq ? in_19 : 32'bz;  // Controlled_Buffer controlled_buffer_73
  assign s11 = comparator_10_eq ? in_21 : 32'bz;  // Controlled_Buffer controlled_buffer_74
  assign s12 = comparator_11_eq ? in_23 : 32'bz;  // Controlled_Buffer controlled_buffer_75
  assign s13 = comparator_12_eq ? in_25 : 32'bz;  // Controlled_Buffer controlled_buffer_76
  assign s14 = comparator_13_eq ? in_27 : 32'bz;  // Controlled_Buffer controlled_buffer_77
  assign s15 = comparator_14_eq ? in_29 : 32'bz;  // Controlled_Buffer controlled_buffer_78
  assign s16 = comparator_15_eq ? in_31 : 32'bz;  // Controlled_Buffer controlled_buffer_79
  assign s17 = comparator_16_eq ? in_33 : 32'bz;  // Controlled_Buffer controlled_buffer_80
  assign s18 = comparator_17_eq ? in_35 : 32'bz;  // Controlled_Buffer controlled_buffer_81
  assign s19 = comparator_18_eq ? in_37 : 32'bz;  // Controlled_Buffer controlled_buffer_82
  assign s20 = comparator_19_eq ? in_39 : 32'bz;  // Controlled_Buffer controlled_buffer_83
  assign s21 = comparator_20_eq ? in_41 : 32'bz;  // Controlled_Buffer controlled_buffer_84
  assign s22 = comparator_21_eq ? in_43 : 32'bz;  // Controlled_Buffer controlled_buffer_85
  assign s23 = comparator_22_eq ? in_45 : 32'bz;  // Controlled_Buffer controlled_buffer_86
  assign s24 = comparator_23_eq ? in_47 : 32'bz;  // Controlled_Buffer controlled_buffer_87
  assign s25 = comparator_24_eq ? in_49 : 32'bz;  // Controlled_Buffer controlled_buffer_88
  assign s26 = comparator_25_eq ? in_51 : 32'bz;  // Controlled_Buffer controlled_buffer_89
  assign s27 = comparator_26_eq ? in_53 : 32'bz;  // Controlled_Buffer controlled_buffer_90
  assign s28 = comparator_27_eq ? in_55 : 32'bz;  // Controlled_Buffer controlled_buffer_91
  assign s29 = comparator_28_eq ? in_57 : 32'bz;  // Controlled_Buffer controlled_buffer_92
  assign s30 = comparator_29_eq ? in_59 : 32'bz;  // Controlled_Buffer controlled_buffer_93
  assign s31 = comparator_30_eq ? in_61 : 32'bz;  // Controlled_Buffer controlled_buffer_94
  assign s32 = comparator_31_eq ? in_63 : 32'bz;  // Controlled_Buffer controlled_buffer_95
  assign s1 = comparator_32_eq ? in_1 : 32'bz;  // Controlled_Buffer controlled_buffer_96
  Adder #(.width(32)) adder_1 (.a(controlled_buffer_1_out), .b(controlled_buffer_2_out), .out(s2));  // open: cin, cout
  Adder #(.width(32)) adder_2 (.a(controlled_buffer_3_out), .b(controlled_buffer_4_out), .out(s3));  // open: cin, cout
  Adder #(.width(32)) adder_3 (.a(controlled_buffer_5_out), .b(controlled_buffer_6_out), .out(s4));  // open: cin, cout
  Adder #(.width(32)) adder_4 (.a(controlled_buffer_7_out), .b(controlled_buffer_8_out), .out(s5));  // open: cin, cout
  Adder #(.width(32)) adder_5 (.a(controlled_buffer_9_out), .b(controlled_buffer_10_out), .out(s6));  // open: cin, cout
  Adder #(.width(32)) adder_6 (
    .a(controlled_buffer_11_out), .b(controlled_buffer_12_out), .out(s7));  // open: cin, cout
  Adder #(.width(32)) adder_7 (
    .a(controlled_buffer_13_out), .b(controlled_buffer_14_out), .out(s8));  // open: cin, cout
  Adder #(.width(32)) adder_8 (
    .a(controlled_buffer_15_out), .b(controlled_buffer_16_out), .out(s9));  // open: cin, cout
  Adder #(.width(32)) adder_9 (
    .a(controlled_buffer_17_out), .b(controlled_buffer_18_out), .out(s10));  // open: cin, cout
  Adder #(.width(32)) adder_10 (
    .a(controlled_buffer_19_out), .b(controlled_buffer_20_out), .out(s11));  // open: cin, cout
  Adder #(.width(32)) adder_11 (
    .a(controlled_buffer_21_out), .b(controlled_buffer_22_out), .out(s12));  // open: cin, cout
  Adder #(.width(32)) adder_12 (
    .a(controlled_buffer_23_out), .b(controlled_buffer_24_out), .out(s13));  // open: cin, cout
  Adder #(.width(32)) adder_13 (
    .a(controlled_buffer_25_out), .b(controlled_buffer_26_out), .out(s14));  // open: cin, cout
  Adder #(.width(32)) adder_14 (
    .a(controlled_buffer_27_out), .b(controlled_buffer_28_out), .out(s15));  // open: cin, cout
  Adder #(.width(32)) adder_15 (
    .a(controlled_buffer_29_out), .b(controlled_buffer_30_out), .out(s16));  // open: cin, cout
  Adder #(.width(32)) adder_16 (
    .a(controlled_buffer_31_out), .b(controlled_buffer_32_out), .out(s17));  // open: cin, cout
  Adder #(.width(32)) adder_17 (
    .a(controlled_buffer_33_out), .b(controlled_buffer_34_out), .out(s18));  // open: cin, cout
  Adder #(.width(32)) adder_18 (
    .a(controlled_buffer_35_out), .b(controlled_buffer_36_out), .out(s19));  // open: cin, cout
  Adder #(.width(32)) adder_19 (
    .a(controlled_buffer_37_out), .b(controlled_buffer_38_out), .out(s20));  // open: cin, cout
  Adder #(.width(32)) adder_20 (
    .a(controlled_buffer_39_out), .b(controlled_buffer_40_out), .out(s21));  // open: cin, cout
  Adder #(.width(32)) adder_21 (
    .a(controlled_buffer_41_out), .b(controlled_buffer_42_out), .out(s22));  // open: cin, cout
  Adder #(.width(32)) adder_22 (
    .a(controlled_buffer_43_out), .b(controlled_buffer_44_out), .out(s23));  // open: cin, cout
  Adder #(.width(32)) adder_23 (
    .a(controlled_buffer_45_out), .b(controlled_buffer_46_out), .out(s24));  // open: cin, cout
  Adder #(.width(32)) adder_24 (
    .a(controlled_buffer_47_out), .b(controlled_buffer_48_out), .out(s25));  // open: cin, cout
  Adder #(.width(32)) adder_25 (
    .a(controlled_buffer_49_out), .b(controlled_buffer_50_out), .out(s26));  // open: cin, cout
  Adder #(.width(32)) adder_26 (
    .a(controlled_buffer_51_out), .b(controlled_buffer_52_out), .out(s27));  // open: cin, cout
  Adder #(.width(32)) adder_27 (
    .a(controlled_buffer_53_out), .b(controlled_buffer_54_out), .out(s28));  // open: cin, cout
  Adder #(.width(32)) adder_28 (
    .a(controlled_buffer_55_out), .b(controlled_buffer_56_out), .out(s29));  // open: cin, cout
  Adder #(.width(32)) adder_29 (
    .a(controlled_buffer_57_out), .b(controlled_buffer_58_out), .out(s30));  // open: cin, cout
  Adder #(.width(32)) adder_30 (
    .a(controlled_buffer_59_out), .b(controlled_buffer_60_out), .out(s31));  // open: cin, cout
  Adder #(.width(32)) adder_31 (
    .a(controlled_buffer_61_out), .b(controlled_buffer_62_out), .out(s32));  // open: cin, cout
  Adder #(.width(32)) adder_32 (
    .a(controlled_buffer_63_out), .b(controlled_buffer_64_out), .out(s1));  // open: cin, cout
endmodule

module distro (
  input  [31:0] in_1,
  input  [31:0] in_2,
  output out_3
);

  wire [31:0] and_1_out;

  assign and_1_out = in_1 & in_2;  // AND_Gate and_1, 32 bits wide
  or or_1 (out_3, and_1_out[0], and_1_out[1], and_1_out[2], and_1_out[3], and_1_out[4], and_1_out[5], and_1_out[6], and_1_out[7], and_1_out[8], and_1_out[9], and_1_out[10], and_1_out[11], and_1_out[12], and_1_out[13], and_1_out[14], and_1_out[15], and_1_out[17], and_1_out[18], and_1_out[19], and_1_out[20], and_1_out[21], and_1_out[22], and_1_out[23], and_1_out[24], and_1_out[25], and_1_out[26], and_1_out[27], and_1_out[28], and_1_out[29], and_1_out[30], and_1_out[31], and_1_out[16]);
endmodule
