// Logisim project Trabalho M3.circ as structural Verilog
module main (
  input  in_1,
  input  Mostrar_msg_descripatada
);

  wire button_1_out, clear_out, keyboard_1_avail, not_1_out, teclado_1_out_2;
  wire [6:0] cifrador_1_leitura, decrypter_1_leitura, keyboard_1_data;

  Button button_1 (.out(button_1_out));
  teclado teclado_1 (.in_1(button_1_out), .out_2(teclado_1_out_2));
  Cifrador cifrador_1 (
    .\clock_gravaçao (teclado_1_out_2), .data(keyboard_1_data), .ld(not_1_out), .leitura(cifrador_1_leitura),
    .in_4(clear_out));
  Keyboard keyboard_1 (.clk(teclado_1_out_2), .re(1'b1), .clr(in_1), .avail(keyboard_1_avail), .data(keyboard_1_data));
  Decrypter decrypter_1 (
    .\clock_gravaçao (teclado_1_out_2), .data(cifrador_1_leitura), .ld(Mostrar_msg_descripatada),
    .leitura(decrypter_1_leitura), .clr(clear_out));
  not not_1 (not_1_out, keyboard_1_avail);
  Button clear (.out(clear_out));
  TTY tty_1 (.data(cifrador_1_leitura), .clk(teclado_1_out_2), .clr(clear_out));  // open: we
  TTY tty_2 (.data(decrypter_1_leitura), .clk(teclado_1_out_2), .clr(clear_out));  // open: we
endmodule

module Cifrador (
  input  \clock_gravaçao ,
  input  [6:0] data,
  input  ld,
  input  in_4,
  output [6:0] leitura
);

  wire comparator_1_eq, not_1_out, not_2_out;
  wire [3:0] counter_1_q, counter_2_q;
  wire [7:0] adder_1_out, controlled_buffer_1_out, ram_1_data;
  wire [7:7] controlled_buffer_4_out;

  Counter #(.width(4), .max('hf)) counter_1 (
    .Q(counter_1_q), .clk(\clock_gravaçao ));  // open: load, D, count, carry, clr
  Adder adder_1 (.a({1'b0, data}), .b(controlled_buffer_1_out), .out(adder_1_out));  // open: cin, cout
  assign controlled_buffer_1_out = comparator_1_eq ? {8{1'b0}} : 8'bz;  // Controlled_Buffer controlled_buffer_1
  assign controlled_buffer_1_out = not_1_out ? {4'b0000, counter_2_q} : 8'bz;  // Controlled_Buffer controlled_buffer_2
  not not_1 (not_1_out, comparator_1_eq);
  Counter #(.width(4), .max('hf)) counter_2 (
    .load(1'b1), .count(1'b1), .Q(counter_2_q), .clk(\clock_gravaçao ));  // open: D, carry, clr
  Comparator comparator_1 (.a({1'b0, data}), .b({8{1'b0}}), .eq(comparator_1_eq));  // open: gt, lt
  RAM #(.addrWidth(4)) ram_1 (
    .addr(counter_1_q), .data(ram_1_data), .clk(\clock_gravaçao ), .ld(ld), .clr(in_4));  // open: sel
  assign ram_1_data = not_2_out ? adder_1_out : 8'bz;  // Controlled_Buffer controlled_buffer_3
  not not_2 (not_2_out, ld);
  assign {controlled_buffer_4_out[7], leitura} = ld ? ram_1_data : 8'bz;  // Controlled_Buffer controlled_buffer_4
endmodule

module teclado (
  input  in_1,
  output out_2
);

  wire clock_1_out;

  Clock clock_1 (.out(clock_1_out));
  and and_1 (out_2, clock_1_out, in_1);
endmodule

module Decrypter (
  input  \clock_gravaçao ,
  input  [6:0] data,
  input  ld,
  input  clr,
  output [6:0] leitura
);

  wire comparator_1_eq, not_1_out, not_2_out;
  wire [3:0] counter_1_q, counter_2_q;
  wire [7:0] controlled_buffer_1_out, ram_1_data, subtractor_1_out;
  wire [7:7] controlled_buffer_4_out;

  Counter #(.width(4), .max('hf)) counter_1 (
    .Q(counter_1_q), .clk(\clock_gravaçao ));  // open: load, D, count, carry, clr
  Subtractor subtractor_1 (.a({1'b0, data}), .b(controlled_buffer_1_out), .out(subtractor_1_out));  // open: bin, bout
  assign controlled_buffer_1_out = comparator_1_eq ? {8{1'b0}} : 8'bz;  // Controlled_Buffer controlled_buffer_1
  assign controlled_buffer_1_out = not_1_out ? {4'b0000, counter_2_q} : 8'bz;  // Controlled_Buffer controlled_buffer_2
  not not_1 (not_1_out, comparator_1_eq);
  Counter #(.width(4), .max('hf)) counter_2 (
    .load(1'b1), .count(1'b1), .Q(counter_2_q), .clk(\clock_gravaçao ));  // open: D, carry, clr
  Comparator comparator_1 (.a({1'b0, data}), .b({8{1'b0}}), .eq(comparator_1_eq));  // open: gt, lt
  RAM #(.addrWidth(4)) ram_1 (
    .addr(counter_1_q), .data(ram_1_data), .clk(\clock_gravaçao ), .ld(ld), .clr(clr));  // open: sel
  assign ram_1_data = not_2_out ? subtractor_1_out : 8'bz;  // Controlled_Buffer controlled_buffer_3
  not not_2 (not_2_out, ld);
  assign {controlled_buffer_4_out[7], leitura} = ld ? ram_1_data : 8'bz;  // Controlled_Buffer controlled_buffer_4
endmodule
